// Logisim project digital_lock_by_Afsana.circ as structural Verilog: 6 circuits, main circuit main
module main (
  input  in_1,
  input  in_2,
  input  [1:0] View_Password
);

  wire _0, _1, _2, _3, _4, _5, _6, _7, _8, _9, bcd_to_7seg_1_a_2, bcd_to_7seg_1_b_2, bcd_to_7seg_1_c_2,
       bcd_to_7seg_1_d_2, bcd_to_7seg_1_e, bcd_to_7seg_1_f, bcd_to_7seg_1_g, bcd_to_7seg_2_a_2,
       bcd_to_7seg_2_b_2, bcd_to_7seg_2_c_2, bcd_to_7seg_2_d_2, bcd_to_7seg_2_e, bcd_to_7seg_2_f,
       bcd_to_7seg_2_g, bcd_to_7seg_3_a_2, bcd_to_7seg_3_b_2, bcd_to_7seg_3_c_2, bcd_to_7seg_3_d_2,
       bcd_to_7seg_3_e, bcd_to_7seg_3_f, bcd_to_7seg_3_g, bcd_to_7seg_4_a_2, bcd_to_7seg_4_b_2,
       bcd_to_7seg_4_c_2, bcd_to_7seg_4_d_2, bcd_to_7seg_4_e, bcd_to_7seg_4_f, bcd_to_7seg_4_g, C0, C1, C2,
       CA, comparator_1_out_17, disp_2_1_c, disp_2_1_d, disp_2_1_e, disp_2_1_g, tunnel;
  wire [3:0] decimal_converter_1_b0, memory_1_out_10_2, memory_1_out_10_3, memory_1_out_11, memory_1_out_12,
       memory_1_out_13, memory_1_out_14, memory_1_out_15, memory_1_out_16, memory_1_out_17, memory_1_out_18,
       memory_1_out_19, memory_1_out_20, memory_1_out_21, memory_1_out_22, memory_1_out_23, memory_1_out_24,
       memory_1_out_25, memory_1_out_26, multiplexer_1_out, multiplexer_2_out, multiplexer_3_out,
       multiplexer_4_out;
  wire [7:0] memory_1_out_10;

  BCD_TO_7seg bcd_to_7seg_1 (
    .A(multiplexer_1_out[3]), .D(multiplexer_1_out[0]), .C(multiplexer_1_out[1]), .a_2(bcd_to_7seg_1_a_2),
    .b_2(bcd_to_7seg_1_b_2), .c_2(bcd_to_7seg_1_c_2), .d_2(bcd_to_7seg_1_d_2), .e(bcd_to_7seg_1_e),
    .f(bcd_to_7seg_1_f), .g(bcd_to_7seg_1_g), .B(multiplexer_1_out[2]));
  Button u__1 (.out(_1));
  Button u__4 (.out(_4));
  Button u__7 (.out(_7));
  Multiplexer #(.width(4), .enable("false")) multiplexer_1 (
    .in0(memory_1_out_10_3), .in1(memory_1_out_23), .out(multiplexer_1_out), .sel(in_1));
  Button u__2 (.out(_2));
  Button u__3 (.out(_3));
  Button u__5 (.out(_5));
  Button u__6 (.out(_6));
  Button u__8 (.out(_8));
  Button u__9 (.out(_9));
  Button u__0 (.out(_0));
  Button Sequential_Delete (.out(tunnel));
  Button Delete_All (.out(CA));
  Button Delete_3rd_Password (.out(C0));
  Button Delete_2nd_Password (.out(C1));
  Button Delete_1st_Password (.out(C2));
  _7_Segment_Display u_7_segment_display_1 (
    .g(bcd_to_7seg_1_g), .f(bcd_to_7seg_1_f), .a(bcd_to_7seg_1_a_2), .b(bcd_to_7seg_1_b_2),
    .e(bcd_to_7seg_1_e), .d(bcd_to_7seg_1_d_2), .c(bcd_to_7seg_1_c_2));  // open: dp
  BCD_TO_7seg bcd_to_7seg_2 (
    .A(multiplexer_2_out[3]), .D(multiplexer_2_out[0]), .C(multiplexer_2_out[1]), .a_2(bcd_to_7seg_2_a_2),
    .b_2(bcd_to_7seg_2_b_2), .c_2(bcd_to_7seg_2_c_2), .d_2(bcd_to_7seg_2_d_2), .e(bcd_to_7seg_2_e),
    .f(bcd_to_7seg_2_f), .g(bcd_to_7seg_2_g), .B(multiplexer_2_out[2]));
  Multiplexer #(.width(4), .enable("false")) multiplexer_2 (
    .in0(memory_1_out_10_2), .in1(memory_1_out_24), .out(multiplexer_2_out), .sel(in_1));
  Decimal_Converter decimal_converter_1 (
    .B0(decimal_converter_1_b0[0]), .B1(decimal_converter_1_b0[1]), .B2(decimal_converter_1_b0[2]),
    .B3(decimal_converter_1_b0[3]), ._9(_9), ._0(_0), ._1(_1), ._2(_2), ._3(_3), ._4(_4), ._5(_5), ._6(_6),
    ._7(_7), ._8(_8));  // open: in_1
  _7_Segment_Display u_7_segment_display_2 (
    .g(bcd_to_7seg_2_g), .f(bcd_to_7seg_2_f), .a(bcd_to_7seg_2_a_2), .b(bcd_to_7seg_2_b_2),
    .e(bcd_to_7seg_2_e), .d(bcd_to_7seg_2_d_2), .c(bcd_to_7seg_2_c_2));  // open: dp
  BCD_TO_7seg bcd_to_7seg_3 (
    .A(multiplexer_3_out[3]), .D(multiplexer_3_out[0]), .C(multiplexer_3_out[1]), .a_2(bcd_to_7seg_3_a_2),
    .b_2(bcd_to_7seg_3_b_2), .c_2(bcd_to_7seg_3_c_2), .d_2(bcd_to_7seg_3_d_2), .e(bcd_to_7seg_3_e),
    .f(bcd_to_7seg_3_f), .g(bcd_to_7seg_3_g), .B(multiplexer_3_out[2]));
  Multiplexer #(.width(4), .enable("false")) multiplexer_3 (
    .in0(memory_1_out_10[7:4]), .in1(memory_1_out_25), .out(multiplexer_3_out), .sel(in_1));
  Memory memory_1 (
    .Input(decimal_converter_1_b0), .User_Mode(in_1), .out_14(memory_1_out_14), .out_17(memory_1_out_17),
    .out_20(memory_1_out_20), .out_23(memory_1_out_23), .out_24(memory_1_out_24), .out_25(memory_1_out_25),
    .out_26(memory_1_out_26), .out_12(memory_1_out_12), .out_15(memory_1_out_15), .out_18(memory_1_out_18),
    .out_21(memory_1_out_21), .out_13(memory_1_out_13), .out_16(memory_1_out_16), .out_19(memory_1_out_19),
    .out_22(memory_1_out_22), .out_11(memory_1_out_11),
    .out_10({memory_1_out_10_3, memory_1_out_10_2, memory_1_out_10}), .Admin(in_2),
    .Output_Selection(View_Password), .Backspace(tunnel), .Clear_all(CA), .Clear_Reg_0(C0), .Clear_Reg_1(C1),
    .Clear_Reg_2(C2));
  _7_Segment_Display u_7_segment_display_3 (
    .g(bcd_to_7seg_3_g), .f(bcd_to_7seg_3_f), .a(bcd_to_7seg_3_a_2), .b(bcd_to_7seg_3_b_2),
    .e(bcd_to_7seg_3_e), .d(bcd_to_7seg_3_d_2), .c(bcd_to_7seg_3_c_2));  // open: dp
  BCD_TO_7seg bcd_to_7seg_4 (
    .A(multiplexer_4_out[3]), .D(multiplexer_4_out[0]), .C(multiplexer_4_out[1]), .a_2(bcd_to_7seg_4_a_2),
    .b_2(bcd_to_7seg_4_b_2), .c_2(bcd_to_7seg_4_c_2), .d_2(bcd_to_7seg_4_d_2), .e(bcd_to_7seg_4_e),
    .f(bcd_to_7seg_4_f), .g(bcd_to_7seg_4_g), .B(multiplexer_4_out[2]));
  Comparator comparator_1 (
    .in_3(memory_1_out_14), .in_5(memory_1_out_17), ._3rd_Bit(memory_1_out_25), .in_7(memory_1_out_20),
    ._4th_Bit(memory_1_out_26), .in_1(memory_1_out_11), .in_9(memory_1_out_12), .in_10(memory_1_out_15),
    .in_11(memory_1_out_18), .in_12(memory_1_out_21), .in_13(memory_1_out_13), .in_14(memory_1_out_16),
    .in_15(memory_1_out_19), .in_16(memory_1_out_22), .out_17(comparator_1_out_17),
    ._2nd_Bit(memory_1_out_24), ._1st_Bit(memory_1_out_23));
  _7_Segment_Display u_7_segment_display_4 (
    .g(bcd_to_7seg_4_g), .f(bcd_to_7seg_4_f), .a(bcd_to_7seg_4_a_2), .b(bcd_to_7seg_4_b_2),
    .e(bcd_to_7seg_4_e), .d(bcd_to_7seg_4_d_2), .c(bcd_to_7seg_4_c_2));  // open: dp
  Multiplexer #(.width(4), .enable("false")) multiplexer_4 (
    .in0(memory_1_out_10[3:0]), .in1(memory_1_out_26), .out(multiplexer_4_out), .sel(in_1));
  Disp_2 disp_2_1 (.A(comparator_1_out_17), .c(disp_2_1_c), .d(disp_2_1_d), .e(disp_2_1_e), .g(disp_2_1_g));
  _7_Segment_Display u_7_segment_display_5 (
    .g(disp_2_1_g), .e(disp_2_1_e), .d(disp_2_1_d), .c(disp_2_1_c));  // open: f, a, b, dp

  // Other names for the same wires on the sheet: A = in_2; M = in_1; S[1:0] = View_Password
endmodule

module BCD_TO_7seg (
  input  A,
  input  D,
  input  C,
  input  B,
  output a_2,
  output b_2,
  output c_2,
  output d_2,
  output e,
  output f,
  output g
);

  wire and_1_out, and_2_out, and_3_out, and_4_out, and_5_out, and_6_out, and_7_out, and_8_out, and_9_out,
       and_10_out, and_11_out, and_12_out, and_13_out, and_14_out, and_15_out, and_16_out, and_17_out,
       and_18_out, and_19_out, and_20_out, and_21_out, and_22_out, and_23_out, not_1_out, not_2_out,
       not_3_out, not_4_out;

  not not_1 (not_1_out, A);
  not not_2 (not_2_out, D);
  not not_3 (not_3_out, C);
  not not_4 (not_4_out, B);
  and and_1 (and_1_out, D, not_4_out);
  and and_2 (and_2_out, not_2_out, B);
  and and_3 (and_3_out, C, B);
  and and_4 (and_4_out, D, not_4_out);
  and and_5 (and_5_out, C, not_4_out);
  and and_6 (and_6_out, not_3_out, B);
  and and_7 (and_7_out, D, not_3_out);
  and and_8 (and_8_out, not_2_out, C);
  and and_9 (and_9_out, A, D);
  and and_10 (and_10_out, A, C);
  and and_11 (and_11_out, D, C);
  and and_12 (and_12_out, not_2_out, B);
  and and_13 (and_13_out, D, not_4_out);
  and and_14 (and_14_out, D, C);
  and and_15 (and_15_out, D, not_4_out);
  and and_16 (and_16_out, A, C);
  and and_17 (and_17_out, C, B);
  and and_18 (and_18_out, D, not_3_out);
  and and_19 (and_19_out, A, D);
  and and_20 (and_20_out, D, C);
  and and_21 (and_21_out, A, C);
  and and_22 (and_22_out, not_1_out, B);
  and and_23 (and_23_out, not_1_out, not_2_out, not_3_out);
  or or_1 (a_2, A, and_1_out, and_2_out, and_3_out);
  or or_2 (b_2, A, and_4_out, and_5_out, and_6_out);
  or or_3 (c_2, A, and_7_out, and_8_out, B);
  or or_4 (d_2, and_9_out, and_10_out, and_11_out, and_12_out, and_13_out);
  or or_5 (e, and_14_out, and_15_out);
  or or_6 (f, and_16_out, and_17_out, and_18_out);
  or or_7 (g, and_19_out, and_20_out, and_21_out, and_22_out, and_23_out);
endmodule

module Disp_2 (
  input  A,
  output c,
  output d,
  output e,
  output g
);

  wire not_1_out;

  not not_1 (not_1_out, A);
  or or_1 (c, A, not_1_out);
  or or_2 (e, A, not_1_out);
  or or_3 (g, not_1_out, A);

  assign d = A;
endmodule

module Memory (
  input  [3:0] Input,
  input  User_Mode,
  input  Admin,
  input  [1:0] Output_Selection,
  input  Clear_Reg_0,
  input  Clear_Reg_1,
  input  Clear_all,
  input  Clear_Reg_2,
  input  Backspace,
  output [15:0] out_10,
  output [3:0] out_11,
  output [3:0] out_12,
  output [3:0] out_13,
  output [3:0] out_14,
  output [3:0] out_15,
  output [3:0] out_16,
  output [3:0] out_17,
  output [3:0] out_18,
  output [3:0] out_19,
  output [3:0] out_20,
  output [3:0] out_21,
  output [3:0] out_22,
  output [3:0] out_23,
  output [3:0] out_24,
  output [3:0] out_25,
  output [3:0] out_26
);

  wire and_1_out, and_2_out, and_3_out, and_4_out, and_5_out, demultiplexer_2_out0, demultiplexer_2_out1,
       or_1_out, or_2_out, or_3_out, or_4_out;
  wire [1:0] multiplexer_2_out;
  wire [3:0] demultiplexer_1_out0, demultiplexer_1_out1, shift_register_1_out, shift_register_3_out;

  Demultiplexer #(.width(4), .enable("false")) demultiplexer_1 (
    .out0(demultiplexer_1_out0), .out1(demultiplexer_1_out1), .in(Input), .sel(User_Mode));
  Demultiplexer #(.enable("false")) demultiplexer_2 (
    .out0(demultiplexer_2_out0), .out1(demultiplexer_2_out1), .in(or_1_out), .sel(User_Mode));
  and and_1 (and_1_out, Admin, Backspace);
  or or_1 (or_1_out, Input[0], Input[1], Input[2], Input[3], and_1_out);
  Shift_Register #(.width(4), .length(4)) shift_register_1 (
    .in(demultiplexer_1_out0), .clk(demultiplexer_2_out0), .out(shift_register_1_out), .clr(or_2_out),
    .q0(out_20), .q1(out_17), .q2(out_14), .q3(out_11));  // open: shift, load, d0, d1, d2, d3
  or or_2 (or_2_out, and_2_out, and_4_out);
  Shift_Register #(.width(4), .length(4)) shift_register_2 (
    .in(demultiplexer_1_out1), .clk(demultiplexer_2_out1), .q0(out_26), .q1(out_25), .q2(out_24), .q3(out_23));  // open: shift, out, load, clr, d0, d1, d2, d3
  and and_2 (and_2_out, Clear_Reg_0, Admin);
  Shift_Register #(.width(4), .length(4)) shift_register_3 (
    .in(shift_register_1_out), .clk(demultiplexer_2_out0), .out(shift_register_3_out), .clr(or_3_out),
    .q0(out_21), .q1(out_18), .q2(out_15), .q3(out_12));  // open: shift, load, d0, d1, d2, d3
  or or_3 (or_3_out, and_3_out, and_4_out);
  and and_3 (and_3_out, Clear_Reg_1, Admin);
  and and_4 (and_4_out, Clear_all, Admin);
  Shift_Register #(.width(4), .length(4)) shift_register_4 (
    .in(shift_register_3_out), .clk(demultiplexer_2_out0), .clr(or_4_out), .q0(out_22), .q1(out_19),
    .q2(out_16), .q3(out_13));  // open: shift, out, load, d0, d1, d2, d3
  or or_4 (or_4_out, and_5_out, and_4_out);
  and and_5 (and_5_out, Clear_Reg_2, Admin);
  Multiplexer #(.select(2), .width(16)) multiplexer_1 (
    .in0({out_11, out_14, out_17, out_20}), .in1({out_12, out_15, out_18, out_21}),
    .in2({out_13, out_16, out_19, out_22}), .out(out_10), .sel(multiplexer_2_out));  // open: in3, en
  Multiplexer #(.width(2)) multiplexer_2 (
    .in0(2'b00), .in1(Output_Selection), .out(multiplexer_2_out), .sel(Admin));  // open: en
endmodule

module Comparator (
  input  [3:0] in_1,
  input  [3:0] _1st_Bit,
  input  [3:0] in_3,
  input  [3:0] _2nd_Bit,
  input  [3:0] in_5,
  input  [3:0] _3rd_Bit,
  input  [3:0] in_7,
  input  [3:0] _4th_Bit,
  input  [3:0] in_9,
  input  [3:0] in_10,
  input  [3:0] in_11,
  input  [3:0] in_12,
  input  [3:0] in_13,
  input  [3:0] in_14,
  input  [3:0] in_15,
  input  [3:0] in_16,
  output out_17
);

  wire and_1_out, and_2_out, and_3_out, comparator_1_eq, comparator_2_eq, comparator_3_eq, comparator_4_eq,
       comparator_5_eq, comparator_6_eq, comparator_7_eq, comparator_8_eq, comparator_9_eq, comparator_10_eq,
       comparator_11_eq, comparator_12_eq;

  Comparator_part #(.width(4)) comparator_1 (.a(in_1), .b(_1st_Bit), .eq(comparator_1_eq));  // open: gt, lt
  Comparator_part #(.width(4)) comparator_2 (.a(in_3), .b(_2nd_Bit), .eq(comparator_2_eq));  // open: gt, lt
  Comparator_part #(.width(4)) comparator_3 (.a(in_5), .b(_3rd_Bit), .eq(comparator_3_eq));  // open: gt, lt
  Comparator_part #(.width(4)) comparator_4 (.a(in_7), .b(_4th_Bit), .eq(comparator_4_eq));  // open: gt, lt
  Comparator_part #(.width(4)) comparator_5 (.a(in_9), .b(_1st_Bit), .eq(comparator_5_eq));  // open: gt, lt
  Comparator_part #(.width(4)) comparator_6 (.a(in_10), .b(_2nd_Bit), .eq(comparator_6_eq));  // open: gt, lt
  Comparator_part #(.width(4)) comparator_7 (.a(in_11), .b(_3rd_Bit), .eq(comparator_7_eq));  // open: gt, lt
  Comparator_part #(.width(4)) comparator_8 (.a(in_12), .b(_4th_Bit), .eq(comparator_8_eq));  // open: gt, lt
  Comparator_part #(.width(4)) comparator_9 (.a(in_13), .b(_1st_Bit), .eq(comparator_9_eq));  // open: gt, lt
  Comparator_part #(.width(4)) comparator_10 (.a(in_14), .b(_2nd_Bit), .eq(comparator_10_eq));  // open: gt, lt
  Comparator_part #(.width(4)) comparator_11 (.a(in_15), .b(_3rd_Bit), .eq(comparator_11_eq));  // open: gt, lt
  Comparator_part #(.width(4)) comparator_12 (.a(in_16), .b(_4th_Bit), .eq(comparator_12_eq));  // open: gt, lt
  and and_1 (and_1_out, comparator_1_eq, comparator_2_eq, comparator_3_eq, comparator_4_eq);
  and and_2 (and_2_out, comparator_5_eq, comparator_6_eq, comparator_7_eq, comparator_8_eq);
  and and_3 (and_3_out, comparator_9_eq, comparator_10_eq, comparator_11_eq, comparator_12_eq);
  or or_1 (out_17, and_1_out, and_2_out, and_3_out);
endmodule

module Decimal_Converter (
  input  in_1,
  input  _0,
  input  _1,
  input  _2,
  input  _3,
  input  _4,
  input  _5,
  input  _6,
  input  _7,
  input  _8,
  input  _9,
  output B0,
  output B1,
  output B2,
  output B3
);

  or or_1 (B0, _0, _2, _4, _6, _8);
  or or_2 (B1, _1, _2, _9, _5, _6);
  or or_3 (B2, _3, _4, _5, _6);
  or or_4 (B3, _7, _9, _8);
endmodule
